# Fritzing sketch sketch (saved by Fritzing 1.0.1rc)

parts:
  Raspberry_Pi1 = Raspberry Pi Zero
  U2 = Mini-360 DC-DC Buck converter [package=THT]
  M1 = linear actuator [package=THT]
  U1 = 2-Channel 5v Relay Shield [package=relay-2ch5v10a]
  Power_plug1 = Power plug

nets:
  N1: Raspberry_Pi1.GIPO15, U1.IN2
  N2: Raspberry_Pi1.GIPO14, U1.IN1
  GND: Raspberry_Pi1.GND, U1.GND
  5V: Raspberry_Pi1.5V, U1.VCC
  N3: U2.IN-, U1.K1-On, U1.K2-On, Power_plug1.GND
  N4: U2.IN+, U1.K1-Off, U1.K2-Off, Power_plug1.VCC
  N5: U2.OUT-, U1.JD-GND
  N6: M1.pin1, U1.K2-In
  N7: M1.pin2, U1.K1-In

custom parts:
  Raspberry Pi Zero: The Raspberry Pi Zero is the latest single board computer to be released by the Raspberry Pi Foundation. It is the entry level model Raspberry Pi perfect for hobbyists, makers and industrial engineers looking to create solutions where small size and low power consumption are important. This is especially relevant for applications in the wearables space as well as up and coming applications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
  Mini-360 DC-DC Buck converter: Mini-360 DC-DC Buck converter. Tiny buck step down voltage converter, input voltage 4.75 to 23V output 1 to 17V adjustable. Available from ebay and the like.
  linear actuator: Generic linear actuator.
  2-Channel 5v Relay Shield: 2 Channel 5v Relay Shield w. 2x SPD-06VDC-SD-C
